// Logisim project cronometro.circ as structural Verilog: 17 circuits, main circuit Cronometro
module Cronometro (
);

  wire A_1, A_2, A_3, A_4, A_5, A_6, and_2_out, and_3_out, and_4_out, and_5_out, and_6_out, and_7_out,
       and_8_out, and_9_out, B_1, B_2, B_3, B_4, B_5, B_6, C_1, C_2, C_3, C_4, C_5, C_6, CB_1, CB_2, CB_3,
       CB_4, CB_5, CB_6, Clockers, Cresce, Cresce_Pulse, D_1, D_2, D_3, D_4, D_5, D_6, DIGITA_0_out,
       DIGITA_1_out, E_1, E_2, E_3, E_4, E_5, E_6, EN, F_1, F_2, F_3, F_4, F_5, F_6, G_1, G_2, G_3, G_4, G_5,
       G_6, Horas, Liga, Liga_Display, Liga_Pulse, Manual, Manual_Automatico_out, Manual_Pulse, Minutos,
       multivibrador_1_saida, my_mux_down_1_saida, my_mux_down_2_saida, my_mux_down_3_saida,
       my_mux_down_4_saida, my_mux_up_1_saida, my_mux_up_2_saida, my_mux_up_3_saida, my_mux_up_4_saida,
       my_mux_up_5_saida, my_mux_up_6_saida, not_1_out, not_2_out, not_3_out, num_02_1_out_5, num_03_1_out_5,
       or_1_out, or_2_out, or_4_out, or_5_out, or_6_out, or_7_out, or_8_out, or_9_out, or_10_out, Q1_1, Q1_2,
       Q1_3, Q1_4, Q1_5, Q1_6, Q2_1, Q2_2, Q2_3, Q2_4, Q2_5, Q2_6, Q3_1, Q3_2, Q3_3, Q3_4, Q3_5, Q3_6, Q4_1,
       Q4_2, Q4_3, Q4_4, Q4_5, Q4_6, Q_CB_1, Q_CB_2, Q_CB_3, Q_CB_4, Q_CB_5, registrador_1_q0,
       registrador_1_q1, registrador_1_q2, registrador_1_q3, Reset, RESET_MUL_out, ResetH, Segundos;
  wire [3:0] Force3;
  wire [3:3] d_ff_6_q;

  Button Liga_Desliga (.out(Liga_Pulse));
  Button Cresce_Descrece (.out(Cresce_Pulse));
  Button Manual_Automatico (.out(Manual_Automatico_out));
  Button u_Reset (.out(Reset));
  Button u_Segundos (.out(Segundos));
  Button u_Minutos (.out(Minutos));
  Button u_Horas (.out(Horas));
  Clock u_Clockers (.out(Clockers));
  Button u_Liga_Display (.out(Liga_Display));
  Alavanca alavanca_1 (.in_1(Liga_Pulse), .out_2(Liga));
  Alavanca alavanca_2 (.in_1(Cresce_Pulse), .out_2(Cresce));
  Alavanca alavanca_3 (.in_1(Manual_Automatico_out), .out_2(Manual));
  and and_1 (Manual_Pulse, Manual, Manual_Automatico_out);
  _7_Segment_Display #(.decimalPoint("false")) u_7_segment_display_1 (
    .g(G_6), .f(F_6), .a(A_6), .b(B_6), .e(E_6), .d(D_6), .c(C_6));
  _7_Segment_Display #(.decimalPoint("false")) u_7_segment_display_2 (
    .g(G_5), .f(F_5), .a(A_5), .b(B_5), .e(E_5), .d(D_5), .c(C_5));
  _7_Segment_Display #(.decimalPoint("false")) u_7_segment_display_3 (
    .g(G_4), .f(F_4), .a(A_4), .b(B_4), .e(E_4), .d(D_4), .c(C_4));
  _7_Segment_Display #(.decimalPoint("false")) u_7_segment_display_4 (
    .g(G_3), .f(F_3), .a(A_3), .b(B_3), .e(E_3), .d(D_3), .c(C_3));
  _7_Segment_Display #(.decimalPoint("false")) u_7_segment_display_5 (
    .g(G_2), .f(F_2), .a(A_2), .b(B_2), .e(E_2), .d(D_2), .c(C_2));
  Button DIGITA_1 (.out(DIGITA_1_out));
  CountMOD10 countmod10_1 (
    .Cresce_Descrece(Cresce), .Reset(Reset), .Impulso(Segundos), .Clock(Clockers),
    .Manual_Automatico(Manual), .Liga(Liga), .Carry_Borrow(CB_1), .Q1(Q1_1), .Q2(Q2_1), .Q3(Q3_1), .Q4(Q4_1));  // open: Force_Num, Reset_Custom
  _7_Segment_Display #(.decimalPoint("false")) u_7_segment_display_6 (
    .g(G_1), .f(F_1), .a(A_1), .b(B_1), .e(E_1), .d(D_1), .c(C_1));
  Registrador registrador_1 (
    .INSERE_1(DIGITA_1_out), .INSERE_0(DIGITA_0_out), .RESET(RESET_MUL_out), .Q0(registrador_1_q0),
    .Q1(registrador_1_q1), .Q2(registrador_1_q2), .Q3(registrador_1_q3));
  Button DIGITA_0 (.out(DIGITA_0_out));
  Button RESET_MUL (.out(RESET_MUL_out));
  LED led_1 (.in(registrador_1_q3));
  LED led_2 (.in(registrador_1_q2));
  D_Flip_Flop d_ff_1 (.D(CB_1), .clk(my_mux_up_1_saida), .Q(Q_CB_1), .reset(or_1_out));  // open: Qn, preset
  My_Mux_Up my_mux_up_1 (.Entrada_0(Clockers), .Entrada_1(Segundos), .Select_0(Manual), .Saida(my_mux_up_1_saida));
  LED led_3 (.in(registrador_1_q0));
  LED led_4 (.in(registrador_1_q1));
  or or_1 (or_1_out, Reset, Manual_Pulse, Cresce_Pulse);
  and and_2 (and_2_out, Clockers, Liga, not_1_out);
  or or_2 (or_2_out, Q_CB_2, Liga_Display);
  not not_1 (not_1_out, Manual);
  Multivibrador multivibrador_1 (
    .Reset(or_4_out), .EN(or_2_out), .Clockers(and_2_out), .E0(registrador_1_q0), .E1(registrador_1_q1),
    .E2(registrador_1_q2), .E3(registrador_1_q3), .Saida(multivibrador_1_saida));
  CountMOD6 countmod6_1 (
    .Liga(Liga), .Cresce_Descresce(Cresce), .Reset(Reset), .Impulso(Q_CB_1), .Clock(Q_CB_1),
    .Manual_Automatico(Manual), .Carry_Borrow(CB_2), .Q1(Q1_2), .Q2(Q2_2), .Q3(Q3_2), .Q4(Q4_2));
  or or_3 (EN, multivibrador_1_saida, not_2_out, Manual);
  not not_2 (not_2_out, Liga);
  or or_4 (or_4_out, Reset, Manual_Pulse);
  Display display_1 (
    .EN(EN), .Q1(Q1_6), .Q2(Q2_6), .Q3(Q3_6), .Q4(Q4_6), .D(D_6), .E(E_6), .F(F_6), .A(A_6), .B(B_6),
    .C(C_6), .G(G_6));
  My_Mux_Up my_mux_up_2 (.Entrada_0(Clockers), .Entrada_1(Segundos), .Select_0(Manual), .Saida(my_mux_up_2_saida));
  Display display_2 (
    .EN(EN), .Q1(Q1_5), .Q2(Q2_5), .Q3(Q3_5), .Q4(Q4_5), .D(D_5), .E(E_5), .F(F_5), .A(A_5), .B(B_5),
    .C(C_5), .G(G_5));
  D_Flip_Flop d_ff_2 (.D(and_3_out), .clk(my_mux_up_2_saida), .Q(Q_CB_2), .reset(or_5_out));  // open: Qn, preset
  and and_3 (and_3_out, CB_2, CB_1);
  or or_5 (or_5_out, Reset, Manual_Pulse, Cresce_Pulse);
  Display display_3 (
    .EN(EN), .Q1(Q1_4), .Q2(Q2_4), .Q3(Q3_4), .Q4(Q4_4), .D(D_4), .E(E_4), .F(F_4), .A(A_4), .B(B_4),
    .C(C_4), .G(G_4));
  CountMOD10 countmod10_2 (
    .Cresce_Descrece(Cresce), .Reset(Reset), .Impulso(Minutos), .Clock(Q_CB_2), .Manual_Automatico(Manual),
    .Liga(Liga), .Carry_Borrow(CB_3), .Q1(Q1_3), .Q2(Q2_3), .Q3(Q3_3), .Q4(Q4_3));  // open: Force_Num, Reset_Custom
  Display display_4 (
    .EN(EN), .Q1(Q1_3), .Q2(Q2_3), .Q3(Q3_3), .Q4(Q4_3), .D(D_3), .E(E_3), .F(F_3), .A(A_3), .B(B_3),
    .C(C_3), .G(G_3));
  and and_4 (and_4_out, CB_1, CB_2, CB_3);
  My_Mux_Down my_mux_down_1 (.Entrada_0(and_4_out), .Entrada_1(CB_3), .Select_0(Manual), .Saida(my_mux_down_1_saida));
  My_Mux_Up my_mux_up_3 (.Entrada_0(Clockers), .Entrada_1(Minutos), .Select_0(Manual), .Saida(my_mux_up_3_saida));
  Display display_5 (
    .EN(EN), .Q1(Q1_2), .Q2(Q2_2), .Q3(Q3_2), .Q4(Q4_2), .D(D_2), .E(E_2), .F(F_2), .A(A_2), .B(B_2),
    .C(C_2), .G(G_2));
  D_Flip_Flop d_ff_3 (
    .D(my_mux_down_1_saida), .clk(my_mux_up_3_saida), .Q(Q_CB_3), .reset(or_6_out));  // open: Qn, preset
  or or_6 (or_6_out, Reset, Manual_Pulse, Cresce_Pulse);
  Display display_6 (
    .EN(EN), .Q1(Q1_1), .Q2(Q2_1), .Q3(Q3_1), .Q4(Q4_1), .D(D_1), .E(E_1), .F(F_1), .A(A_1), .B(B_1),
    .C(C_1), .G(G_1));
  CountMOD6 countmod6_2 (
    .Liga(Liga), .Cresce_Descresce(Cresce), .Reset(Reset), .Impulso(Q_CB_3), .Clock(Q_CB_3),
    .Manual_Automatico(Manual), .Carry_Borrow(CB_4), .Q1(Q1_4), .Q2(Q2_4), .Q3(Q3_4), .Q4(Q4_4));
  and and_5 (and_5_out, CB_1, CB_2, CB_3, CB_4);
  My_Mux_Down my_mux_down_2 (.Entrada_0(and_5_out), .Entrada_1(CB_4), .Select_0(Manual), .Saida(my_mux_down_2_saida));
  My_Mux_Up my_mux_up_4 (.Entrada_0(Clockers), .Entrada_1(Minutos), .Select_0(Manual), .Saida(my_mux_up_4_saida));
  D_Flip_Flop d_ff_4 (
    .D(my_mux_down_2_saida), .clk(my_mux_up_4_saida), .Q(Q_CB_4), .reset(or_7_out));  // open: Qn, preset
  or or_7 (or_7_out, Reset, Manual_Pulse, Cresce_Pulse);
  or or_8 (or_8_out, Reset, ResetH);
  CountMOD10 countmod10_3 (
    .Cresce_Descrece(Cresce), .Reset(or_8_out), .Impulso(Horas), .Clock(Q_CB_4), .Manual_Automatico(Manual),
    .Force_Num(Force3), .Reset_Custom(4'b0011), .Liga(Liga), .Carry_Borrow(CB_5), .Q1(Q1_5), .Q2(Q2_5),
    .Q3(Q3_5), .Q4(Q4_5));
  and and_6 (and_6_out, CB_1, CB_2, CB_3, CB_4, CB_5);
  My_Mux_Down my_mux_down_3 (.Entrada_0(and_6_out), .Entrada_1(CB_5), .Select_0(Manual), .Saida(my_mux_down_3_saida));
  My_Mux_Up my_mux_up_5 (.Entrada_0(Clockers), .Entrada_1(Horas), .Select_0(Manual), .Saida(my_mux_up_5_saida));
  D_Flip_Flop d_ff_5 (
    .D(my_mux_down_3_saida), .clk(my_mux_up_5_saida), .Q(Q_CB_5), .reset(or_9_out));  // open: Qn, preset
  or or_9 (or_9_out, Reset, Manual_Pulse, Cresce_Pulse);
  or or_10 (or_10_out, Reset, ResetH);
  and and_7 (and_7_out, Cresce, CB_1, CB_2, CB_3, CB_4, CB_5, CB_6);
  CountMOD3 countmod3_1 (
    .Liga(Liga), .Cresce_Descresce(Cresce), .Reset(or_10_out), .Impulso(Q_CB_5), .Clock(Q_CB_5),
    .Manual_Automatico(Manual), .Carry_Borrow(CB_6), .Q1(Q1_6), .Q2(Q2_6), .Q3(Q3_6), .Q4(Q4_6));
  My_Mux_Down my_mux_down_4 (
    .Entrada_0(and_7_out), .Entrada_1(and_8_out), .Select_0(Manual), .Saida(my_mux_down_4_saida));
  D_Flip_Flop d_ff_6 (
    .D(my_mux_down_4_saida), .clk(my_mux_up_6_saida), .Q(d_ff_6_q[3]), .reset(and_9_out));  // open: Qn, preset
  My_Mux_Up my_mux_up_6 (.Entrada_0(Clockers), .Entrada_1(Horas), .Select_0(Manual), .Saida(my_mux_up_6_saida));
  and and_8 (and_8_out, Cresce, CB_6, CB_5);
  and and_9 (and_9_out, num_02_1_out_5, num_03_1_out_5);
  Num_02 num_02_1 (.in_1(Q1_6), .in_2(Q2_6), .in_3(Q3_6), .in_4(Q4_6), .out_5(num_02_1_out_5));
  Num_03 num_03_1 (.in_1(Q1_5), .in_2(Q2_5), .in_3(Q3_5), .in_4(Q4_5), .out_5(num_03_1_out_5));
  assign Force3 = {4{d_ff_6_q[3]}} & 4'b0011;  // AND_Gate and_10, 4 bits wide
  not not_3 (not_3_out, Cresce);
  and and_11 (ResetH, Q2_6, Q3_5, not_3_out);

  // Notes on the sheet:
  //   GLOSSÁRIO:
  //   - CB = Carry OU Borrow
  //   ENTRADAS
  //   CRONÔMETRO
  //   :
  //   Segundos Unidade
  //   :
  //   Segundos Dezena
  //   HORAS
  //   DISPLAYS
  //   MINUTOS
  //   Minutos Unidade
  //   SEGUNDOS
  //   Minutos Dezena
  //   Horas Unidade
  //   Horas Dezena
  //   24h Decrescente
  //   Se H = 00 => reset pra 23 no PRÓXIMO clock
  //   24h Crescente
  //   Se H = 24 => reset pra 00
endmodule

module Display (
  input  EN,
  input  Q1,
  input  Q2,
  input  Q3,
  input  Q4,
  output A,
  output B,
  output C,
  output D,
  output E,
  output F,
  output G
);

  wire and_1_out, and_2_out, and_3_out, and_4_out, and_5_out, and_6_out, and_7_out, and_8_out, and_9_out,
       and_10_out, and_11_out, and_12_out, not_1_out, not_2_out, not_3_out, or_1_out, or_2_out, or_3_out,
       or_4_out, or_5_out, or_6_out, or_7_out, xnor_1_out, xnor_2_out;

  not not_1 (not_1_out, Q1);
  not not_2 (not_2_out, Q2);
  not not_3 (not_3_out, Q3);
  // NOT_Gate not_4 has open pins: in=Q4, out=open
  xnor xnor_1 (xnor_1_out, Q1, Q3);
  xnor xnor_2 (xnor_2_out, Q1, Q2);
  and and_1 (and_1_out, Q2, not_1_out);
  and and_2 (and_2_out, Q2, not_3_out);
  and and_3 (and_3_out, not_3_out, not_1_out);
  and and_4 (and_4_out, Q1, not_2_out, Q3);
  and and_5 (and_5_out, not_1_out, not_3_out);
  and and_6 (and_6_out, Q2, not_1_out);
  and and_7 (and_7_out, not_2_out, Q3);
  and and_8 (and_8_out, not_2_out, not_1_out);
  and and_9 (and_9_out, not_1_out, Q3);
  and and_10 (and_10_out, Q2, not_3_out);
  and and_11 (and_11_out, not_2_out, Q3);
  and and_12 (and_12_out, Q2, not_1_out);
  or or_1 (or_1_out, Q4, Q2, xnor_1_out);
  or or_2 (or_2_out, not_3_out, xnor_2_out);
  or or_3 (or_3_out, not_2_out, Q1, Q3);
  or or_4 (or_4_out, Q4, and_1_out, and_2_out, and_3_out, and_4_out);
  or or_5 (or_5_out, and_5_out, and_6_out);
  or or_6 (or_6_out, Q4, and_7_out, and_8_out, and_9_out);
  or or_7 (or_7_out, Q4, and_10_out, and_11_out, and_12_out);
  and and_13 (A, EN, or_1_out);
  and and_14 (B, EN, or_2_out);
  and and_15 (C, EN, or_3_out);
  and and_16 (D, EN, or_4_out);
  and and_17 (E, EN, or_5_out);
  and and_18 (F, EN, or_6_out);
  and and_19 (G, EN, or_7_out);
endmodule

module CountMOD3 (
  input  Cresce_Descresce,
  input  Reset,
  input  Impulso,
  input  Liga,
  input  Clock,
  input  Manual_Automatico,
  output Carry_Borrow,
  output Q1,
  output Q3,
  output Q2,
  output Q4
);

  wire and_1_out, and_2_out, D1, D1_pre, D2, D2_pre, D3, D4, Its_0, Its_2, my_mux_up_1_saida, nor_1_out,
       nor_2_out, not_1_out, R1, R2, R3, R4, S1, S2, S3, S4;
  wire [3:0] my_mux_4bits_2_saida, my_mux_4bits_4_saida, not_5_out;

  Num_00 num_00_1 (.in_1(Q1), .in_2(Q2), .in_3(Q3), .in_4(Q4), .out_5(Its_0));
  Num_02 num_02_1 (.in_1(Q1), .in_2(Q2), .in_3(Q3), .in_4(Q4), .out_5(Its_2));
  nor nor_1 (nor_1_out, Q1, Q2);
  My_Mux_Down my_mux_down_1 (.Entrada_0(nor_1_out), .Entrada_1(Q2), .Select_0(Cresce_Descresce), .Saida(D1_pre));
  D_Flip_Flop d_ff_1 (.D(D1), .clk(my_mux_up_1_saida), .Q(Q1), .preset(S1), .reset(R1));  // open: Qn
  D_Flip_Flop d_ff_2 (.D(D2), .clk(my_mux_up_1_saida), .Q(Q2), .preset(S2), .reset(R2));  // open: Qn
  My_Mux_Up my_mux_up_1 (
    .Entrada_0(Clock), .Entrada_1(Impulso), .Select_0(Manual_Automatico), .Saida(my_mux_up_1_saida));
  My_Mux_Down my_mux_down_2 (.Entrada_0(Q1), .Entrada_1(nor_2_out), .Select_0(Cresce_Descresce), .Saida(D2_pre));
  D_Flip_Flop d_ff_3 (.D(D3), .clk(my_mux_up_1_saida), .Q(Q3), .preset(S3), .reset(R3));  // open: Qn
  not not_1 (not_1_out, Cresce_Descresce);
  and and_1 (and_1_out, not_1_out, Its_2);
  and and_2 (and_2_out, Cresce_Descresce, Its_0);
  nor nor_2 (nor_2_out, Q1, Q2);
  D_Flip_Flop d_ff_4 (.D(D4), .clk(my_mux_up_1_saida), .Q(Q4), .preset(S4), .reset(R4));  // open: Qn
  or or_1 (Carry_Borrow, and_1_out, and_2_out);
  My_Mux_Down my_mux_down_3 (.Entrada_0(Q1), .Entrada_1(D1_pre), .Select_0(Liga), .Saida(D1));
  My_Mux_4bits my_mux_4bits_1 (
    .Entrada_0(4'b0000), .Entrada_1(my_mux_4bits_2_saida), .Select_0(Reset), .Saida({S4, S3, S2, S1}));
  My_Mux_4bits my_mux_4bits_2 (
    .Entrada_0(4'b0000), .Entrada_1(4'b0010), .Select_0(Cresce_Descresce), .Saida(my_mux_4bits_2_saida));
  My_Mux_Down my_mux_down_4 (.Entrada_0(Q2), .Entrada_1(D2_pre), .Select_0(Liga), .Saida(D2));
  My_Mux_Down my_mux_down_5 (.Entrada_0(Q3), .Entrada_1(1'b0), .Select_0(Liga), .Saida(D3));
  My_Mux_4bits my_mux_4bits_3 (.Entrada_0(4'b0000), .Entrada_1(not_5_out), .Select_0(Reset), .Saida({R4, R3, R2, R1}));
  My_Mux_Down my_mux_down_6 (.Entrada_0(Q4), .Entrada_1(1'b0), .Select_0(Liga), .Saida(D4));
  not not_2 (not_5_out[3], my_mux_4bits_4_saida[3]);
  not not_3 (not_5_out[2], my_mux_4bits_4_saida[2]);
  not not_4 (not_5_out[1], my_mux_4bits_4_saida[1]);
  not not_5 (not_5_out[0], my_mux_4bits_4_saida[0]);
  My_Mux_4bits my_mux_4bits_4 (
    .Entrada_0(4'b0000), .Entrada_1(4'b0010), .Select_0(Cresce_Descresce), .Saida(my_mux_4bits_4_saida));

  // Other names for the same wires on the sheet: Cresce = Cresce_Descresce; Manual = Manual_Automatico

  // Notes on the sheet:
  //   ZERO = 0000
  //   DOIS = 1100
  //   CRESCENTE
  //   Cresce = 0 => Crescente
  //   Cresce = 1 => Decrescente
  //   Se é ZERO ou DOIS
  //   DESCRESCENTE
  //   Manual = 0 => CLOCK
  //   Manual = 1 => IMPULSO
  //   CRESCENTE
  //   DESCRESCENTE
  //   É crescente e NUM = 2 => CARRY
  //   É decrescente e NUM = 0 => Borrow
  //   PINOS do SET
  //   Se desligado, mantém o valor de Q, ou seja, não altera
  //   Se RESET + Crescente => volta pra ZERO
  //   Se RESET + Descrescente => volta pra DOIS
  //   PINOS do RESET
  //   Saídas
endmodule

module CountMOD6 (
  input  Cresce_Descresce,
  input  Reset,
  input  Impulso,
  input  Liga,
  input  Clock,
  input  Manual_Automatico,
  output Carry_Borrow,
  output Q1,
  output Q3,
  output Q2,
  output Q4
);

  wire and_1_out, and_2_out, and_3_out, and_4_out, and_5_out, and_6_out, and_7_out, and_8_out, and_9_out,
       and_10_out, D1, D1_pre, D2, D2_pre, D3, D3_pre, D4, Its_0, Its_5, my_mux_up_1_saida, not_2_out,
       not_3_out, not_4_out, or_1_out, or_2_out, or_4_out, or_5_out, R1, R2, R3, R4, S1, S2, S3, S4;
  wire [3:0] my_mux_4bits_2_saida, my_mux_4bits_4_saida, not_8_out;

  not not_1 (D1_pre, Q1);
  not not_2 (not_2_out, Q2);
  not not_3 (not_3_out, Q3);
  and and_1 (and_1_out, D1_pre, Q2);
  Num_00 num_00_1 (.in_1(Q1), .in_2(Q2), .in_3(Q3), .in_4(Q4), .out_5(Its_0));
  Num_05 num_05_1 (.in_1(Q1), .in_2(Q2), .in_3(Q3), .in_4(Q4), .out_5(Its_5));
  or or_1 (or_1_out, and_1_out, and_2_out);
  and and_2 (and_2_out, Q1, not_2_out, not_3_out);
  My_Mux_Down my_mux_down_1 (.Entrada_0(or_1_out), .Entrada_1(or_2_out), .Select_0(Cresce_Descresce), .Saida(D2_pre));
  D_Flip_Flop d_ff_1 (.D(D1), .clk(my_mux_up_1_saida), .Q(Q1), .preset(S1), .reset(R1));  // open: Qn
  and and_3 (and_3_out, Q1, Q2);
  D_Flip_Flop d_ff_2 (.D(D2), .clk(my_mux_up_1_saida), .Q(Q2), .preset(S2), .reset(R2));  // open: Qn
  My_Mux_Up my_mux_up_1 (
    .Entrada_0(Clock), .Entrada_1(Impulso), .Select_0(Manual_Automatico), .Saida(my_mux_up_1_saida));
  or or_2 (or_2_out, and_3_out, and_4_out);
  D_Flip_Flop d_ff_3 (.D(D3), .clk(my_mux_up_1_saida), .Q(Q3), .preset(S3), .reset(R3));  // open: Qn
  not not_4 (not_4_out, Cresce_Descresce);
  and and_4 (and_4_out, D1_pre, Q3);
  D_Flip_Flop d_ff_4 (.D(D4), .clk(my_mux_up_1_saida), .Q(Q4), .preset(S4), .reset(R4));  // open: Qn
  and and_5 (and_5_out, not_4_out, Its_5);
  and and_6 (and_6_out, Cresce_Descresce, Its_0);
  or or_3 (Carry_Borrow, and_5_out, and_6_out);
  and and_7 (and_7_out, Q1, Q2);
  or or_4 (or_4_out, and_7_out, and_8_out);
  My_Mux_Down my_mux_down_2 (.Entrada_0(Q1), .Entrada_1(D1_pre), .Select_0(Liga), .Saida(D1));
  My_Mux_4bits my_mux_4bits_1 (
    .Entrada_0(4'b0000), .Entrada_1(my_mux_4bits_2_saida), .Select_0(Reset), .Saida({S4, S3, S2, S1}));
  My_Mux_4bits my_mux_4bits_2 (
    .Entrada_0(4'b0000), .Entrada_1(4'b0101), .Select_0(Cresce_Descresce), .Saida(my_mux_4bits_2_saida));
  and and_8 (and_8_out, D1_pre, Q3);
  My_Mux_Down my_mux_down_3 (.Entrada_0(or_4_out), .Entrada_1(or_5_out), .Select_0(Cresce_Descresce), .Saida(D3_pre));
  My_Mux_Down my_mux_down_4 (.Entrada_0(Q2), .Entrada_1(D2_pre), .Select_0(Liga), .Saida(D2));
  and and_9 (and_9_out, Q1, Q3);
  My_Mux_Down my_mux_down_5 (.Entrada_0(Q3), .Entrada_1(D3_pre), .Select_0(Liga), .Saida(D3));
  My_Mux_4bits my_mux_4bits_3 (.Entrada_0(4'b0000), .Entrada_1(not_8_out), .Select_0(Reset), .Saida({R4, R3, R2, R1}));
  My_Mux_Down my_mux_down_6 (.Entrada_0(Q4), .Entrada_1(1'b0), .Select_0(Liga), .Saida(D4));
  not not_5 (not_8_out[3], my_mux_4bits_4_saida[3]);
  not not_6 (not_8_out[2], my_mux_4bits_4_saida[2]);
  not not_7 (not_8_out[1], my_mux_4bits_4_saida[1]);
  not not_8 (not_8_out[0], my_mux_4bits_4_saida[0]);
  My_Mux_4bits my_mux_4bits_4 (
    .Entrada_0(4'b0000), .Entrada_1(4'b0101), .Select_0(Cresce_Descresce), .Saida(my_mux_4bits_4_saida));
  or or_5 (or_5_out, and_9_out, and_10_out);
  and and_10 (and_10_out, D1_pre, not_2_out, not_3_out);

  // Other names for the same wires on the sheet: Cresce = Cresce_Descresce; Manual = Manual_Automatico

  // Notes on the sheet:
  //   CRESCENTE
  //   DESCRESCENTE
  //   ZERO = 0000
  //   CINCO = 1010
  //   Cresce = 0 => Crescente
  //   Cresce = 1 => Decrescente
  //   CRESCENTE
  //   Se é ZERO ou CINCO
  //   Manual = 0 => CLOCK
  //   Manual = 1 => IMPULSO
  //   DESCRESCENTE
  //   É crescente e NUM = 9 => CARRY
  //   É decrescente e NUM = 0 => Borrow
  //   CRESCENTE
  //   PINOS do SET
  //   Se desligado, mantém o valor de Q, ou seja, não altera
  //   Se RESET + Crescente => volta pra ZERO
  //   Se RESET + Descrescente => volta pra NOVE
  //   DESCRESCENTE
  //   PINOS do RESET
  //   Saídas
endmodule

module CountMOD10 (
  input  Cresce_Descrece,
  input  Reset,
  input  Impulso,
  input  Liga,
  input  Clock,
  input  Manual_Automatico,
  input  [3:0] Force_Num,
  input  [3:0] Reset_Custom,
  output Carry_Borrow,
  output Q1,
  output Q3,
  output Q2,
  output Q4
);

  wire and_1_out, and_2_out, and_3_out, and_4_out, and_5_out, and_6_out, and_7_out, and_8_out, and_9_out,
       and_10_out, and_11_out, and_12_out, and_14_out, and_15_out, and_16_out, and_17_out, and_18_out, D1,
       D1_pre, D2, D2_pre, D3, D3_pre, D4, D4_pre, Its_0, Its_9, my_mux_up_1_saida, not_2_out, not_3_out,
       not_4_out, not_5_out, or_1_out, or_2_out, or_4_out, or_5_out, or_8_out, or_9_out, or_11_out,
       or_12_out, R1, R2, R3, R4, S1, S2, S3, S4;
  wire [3:0] and_13_out, my_mux_4bits_1_saida, my_mux_4bits_2_saida, my_mux_4bits_3_saida,
       my_mux_4bits_4_saida, my_mux_4bits_5_saida, my_mux_4bits_6_saida, not_9_out, not_10_out;
  wire [3:3] or_10_out;

  not not_1 (D1_pre, Q1);
  not not_2 (not_2_out, Q2);
  not not_3 (not_3_out, Q3);
  not not_4 (not_4_out, Q4);
  and and_1 (and_1_out, D1_pre, Q2);
  Num_00 num_00_1 (.in_1(Q1), .in_2(Q2), .in_3(Q3), .in_4(Q4), .out_5(Its_0));
  Num_09 num_09_1 (.in_1(Q1), .in_2(Q2), .in_3(Q3), .in_4(Q4), .out_5(Its_9));
  or or_1 (or_1_out, and_1_out, and_2_out);
  and and_2 (and_2_out, Q1, not_2_out, not_4_out);
  My_Mux_Down my_mux_down_1 (.Entrada_0(or_1_out), .Entrada_1(or_2_out), .Select_0(Cresce_Descrece), .Saida(D2_pre));
  D_Flip_Flop d_ff_1 (.D(D1), .clk(my_mux_up_1_saida), .Q(Q1), .preset(S1), .reset(R1));  // open: Qn
  and and_3 (and_3_out, Q1, Q2);
  D_Flip_Flop d_ff_2 (.D(D2), .clk(my_mux_up_1_saida), .Q(Q2), .preset(S2), .reset(R2));  // open: Qn
  My_Mux_Up my_mux_up_1 (
    .Entrada_0(Clock), .Entrada_1(Impulso), .Select_0(Manual_Automatico), .Saida(my_mux_up_1_saida));
  and and_4 (and_4_out, D1_pre, not_2_out, Q3);
  or or_2 (or_2_out, and_3_out, and_4_out, and_7_out);
  D_Flip_Flop d_ff_3 (.D(D3), .clk(my_mux_up_1_saida), .Q(Q3), .preset(S3), .reset(R3));  // open: Qn
  not not_5 (not_5_out, Cresce_Descrece);
  and and_5 (and_5_out, not_5_out, Its_9);
  and and_6 (and_6_out, Cresce_Descrece, Its_0);
  and and_7 (and_7_out, D1_pre, not_2_out, Q4);
  D_Flip_Flop d_ff_4 (.D(D4), .clk(my_mux_up_1_saida), .Q(Q4), .preset(S4), .reset(R4));  // open: Qn
  or or_3 (Carry_Borrow, and_5_out, and_6_out);
  and and_8 (and_8_out, Q3, not_2_out);
  or or_4 (or_4_out, Reset_Custom[0], Reset_Custom[1], Reset_Custom[2], Reset_Custom[3]);
  and and_9 (and_9_out, Q3, D1_pre);
  or or_5 (or_5_out, and_8_out, and_9_out, and_10_out);
  My_Mux_Down my_mux_down_2 (.Entrada_0(Q1), .Entrada_1(D1_pre), .Select_0(Liga), .Saida(D1));
  assign {S4, S3, S2, S1} = my_mux_4bits_1_saida | Force_Num;  // OR_Gate or_6, 4 bits wide
  My_Mux_4bits my_mux_4bits_1 (
    .Entrada_0(4'b0000), .Entrada_1(my_mux_4bits_2_saida), .Select_0(Reset), .Saida(my_mux_4bits_1_saida));
  My_Mux_4bits my_mux_4bits_2 (
    .Entrada_0(4'b0000), .Entrada_1(my_mux_4bits_3_saida), .Select_0(Cresce_Descrece),
    .Saida(my_mux_4bits_2_saida));
  My_Mux_4bits my_mux_4bits_3 (
    .Entrada_0(4'b1001), .Entrada_1(Reset_Custom), .Select_0(or_4_out), .Saida(my_mux_4bits_3_saida));
  and and_10 (and_10_out, not_3_out, Q2, Q1);
  My_Mux_Down my_mux_down_3 (.Entrada_0(Q2), .Entrada_1(D2_pre), .Select_0(Liga), .Saida(D2));
  My_Mux_Down my_mux_down_4 (.Entrada_0(or_5_out), .Entrada_1(or_9_out), .Select_0(Cresce_Descrece), .Saida(D3_pre));
  and and_11 (and_11_out, Q1, Q3);
  My_Mux_Down my_mux_down_5 (.Entrada_0(Q3), .Entrada_1(D3_pre), .Select_0(Liga), .Saida(D3));
  My_Mux_Down my_mux_down_6 (.Entrada_0(Q4), .Entrada_1(D4_pre), .Select_0(Liga), .Saida(D4));
  assign {R4, R3, R2, R1} = my_mux_4bits_4_saida | and_13_out;  // OR_Gate or_7, 4 bits wide
  My_Mux_4bits my_mux_4bits_4 (
    .Entrada_0(4'b0000), .Entrada_1(not_9_out), .Select_0(Reset), .Saida(my_mux_4bits_4_saida));
  not not_6 (not_9_out[3], my_mux_4bits_5_saida[3]);
  or or_8 (or_8_out, Reset_Custom[0], Reset_Custom[1], Reset_Custom[2], Reset_Custom[3]);
  and and_12 (and_12_out, Q2, Q3);
  or or_9 (or_9_out, and_11_out, and_12_out, and_14_out);
  assign and_13_out = {4{or_10_out[3]}} & not_10_out;  // AND_Gate and_13, 4 bits wide
  not not_7 (not_9_out[2], my_mux_4bits_5_saida[2]);
  not not_8 (not_9_out[1], my_mux_4bits_5_saida[1]);
  not not_9 (not_9_out[0], my_mux_4bits_5_saida[0]);
  My_Mux_4bits my_mux_4bits_5 (
    .Entrada_0(4'b0000), .Entrada_1(my_mux_4bits_6_saida), .Select_0(Cresce_Descrece),
    .Saida(my_mux_4bits_5_saida));
  My_Mux_4bits my_mux_4bits_6 (
    .Entrada_0(4'b1001), .Entrada_1(Reset_Custom), .Select_0(or_8_out), .Saida(my_mux_4bits_6_saida));
  and and_14 (and_14_out, D1_pre, not_2_out, Q4);
  not not_10 (not_10_out[0], Force_Num[0]);
  not not_11 (not_10_out[1], Force_Num[1]);
  not not_12 (not_10_out[2], Force_Num[2]);
  not not_13 (not_10_out[3], Force_Num[3]);
  and and_15 (and_15_out, Q4, D1_pre);
  or or_10 (or_10_out[3], Force_Num[3], Force_Num[2], Force_Num[1], Force_Num[0]);
  or or_11 (or_11_out, and_15_out, and_16_out);
  and and_16 (and_16_out, Q1, Q2, Q3);
  My_Mux_Down my_mux_down_7 (.Entrada_0(or_11_out), .Entrada_1(or_12_out), .Select_0(Cresce_Descrece), .Saida(D4_pre));
  and and_17 (and_17_out, Q4, Q1);
  or or_12 (or_12_out, and_17_out, and_18_out);
  and and_18 (and_18_out, D1_pre, not_2_out, not_3_out, not_4_out);

  // Other names for the same wires on the sheet: Cresce = Cresce_Descrece; ForceN[3:0] = Force_Num;
  //   Manual = Manual_Automatico; ResetC[3:0] = Reset_Custom

  // Notes on the sheet:
  //   CRESCENTE
  //   DESCRESCENTE
  //   ZERO = 0000
  //   NOVE = 1001
  //   Cresce = 0 => Crescente
  //   Cresce = 1 => Decrescente
  //   Manual = 0 => CLOCK
  //   Manual = 1 => Impulso
  //   Se é ZERO ou NOVE
  //   CRESCENTE
  //   DESCRESCENTE
  //   É crescente e NUM = 9 => CARRY
  //   É decrescente e NUM = 0 => Borrow
  //   CRESCENTE
  //   PINOS do SET
  //   Se desligado, mantém o valor de Q, ou seja, não altera
  //   Se RESET + Crescente => volta pra ZERO
  //   Se RESET + Descrescente => volta pra NOVE
  //   DESCRESCENTE
  //   PINOS do RESET
  //   Saídas
  //   CRESCENTE
  //   DESCRESCENTE
endmodule

module Alavanca (
  input  in_1,
  output out_2
);

  wire d_ff_1_qn;

  D_Flip_Flop d_ff_1 (.D(d_ff_1_qn), .clk(in_1), .Q(out_2), .Qn(d_ff_1_qn));  // open: preset, reset
endmodule

module Num_00 (
  input  in_1,
  input  in_2,
  input  in_3,
  input  in_4,
  output out_5
);

  wire not_1_out, not_2_out, not_3_out, not_4_out;

  not not_1 (not_1_out, in_1);
  not not_2 (not_2_out, in_2);
  not not_3 (not_3_out, in_3);
  not not_4 (not_4_out, in_4);
  and and_1 (out_5, not_1_out, not_2_out, not_3_out, not_4_out);
endmodule

module Num_02 (
  input  in_1,
  input  in_2,
  input  in_3,
  input  in_4,
  output out_5
);

  wire not_1_out, not_2_out, not_3_out;

  not not_1 (not_1_out, in_1);
  not not_2 (not_2_out, in_3);
  not not_3 (not_3_out, in_4);
  and and_1 (out_5, not_1_out, in_2, not_2_out, not_3_out);
endmodule

module Num_03 (
  input  in_1,
  input  in_2,
  input  in_3,
  input  in_4,
  output out_5
);

  wire not_1_out, not_2_out;

  not not_1 (not_1_out, in_3);
  not not_2 (not_2_out, in_4);
  and and_1 (out_5, in_1, in_2, not_1_out, not_2_out);
endmodule

module Num_04 (
  input  in_1,
  input  in_2,
  input  in_3,
  input  in_4,
  output out_5
);

  wire not_1_out, not_2_out, not_3_out;

  not not_1 (not_1_out, in_1);
  not not_2 (not_2_out, in_2);
  not not_3 (not_3_out, in_4);
  and and_1 (out_5, not_1_out, not_2_out, in_3, not_3_out);
endmodule

module Num_05 (
  input  in_1,
  input  in_2,
  input  in_3,
  input  in_4,
  output out_5
);

  wire not_1_out, not_2_out;

  not not_1 (not_1_out, in_2);
  not not_2 (not_2_out, in_4);
  and and_1 (out_5, in_1, not_1_out, in_3, not_2_out);
endmodule

module Num_09 (
  input  in_1,
  input  in_2,
  input  in_3,
  input  in_4,
  output out_5
);

  wire not_1_out, not_2_out;

  not not_1 (not_1_out, in_2);
  not not_2 (not_2_out, in_3);
  and and_1 (out_5, in_1, not_1_out, not_2_out, in_4);
endmodule

module My_Mux_Up (
  input  Entrada_0,
  input  Entrada_1,
  input  Select_0,
  output Saida
);

  wire and_1_out, and_2_out, not_1_out;

  not not_1 (not_1_out, Select_0);
  and and_1 (and_1_out, Entrada_0, not_1_out);
  and and_2 (and_2_out, Entrada_1, Select_0);
  or or_1 (Saida, and_1_out, and_2_out);
endmodule

module My_Mux_Down (
  input  Entrada_0,
  input  Entrada_1,
  input  Select_0,
  output Saida
);

  wire and_1_out, and_2_out, not_1_out;

  not not_1 (not_1_out, Select_0);
  and and_1 (and_1_out, Entrada_0, not_1_out);
  and and_2 (and_2_out, Entrada_1, Select_0);
  or or_1 (Saida, and_1_out, and_2_out);
endmodule

module My_Mux_4bits (
  input  [3:0] Entrada_0,
  input  [3:0] Entrada_1,
  input  Select_0,
  output [3:0] Saida
);

  wire [3:0] and_1_out, and_2_out, not_1_out;

  assign not_1_out = ~{4{Select_0}};  // NOT_Gate not_1, 4 bits wide
  assign and_1_out = Entrada_0 & not_1_out;  // AND_Gate and_1, 4 bits wide
  assign and_2_out = Entrada_1 & {4{Select_0}};  // AND_Gate and_2, 4 bits wide
  assign Saida = and_1_out | and_2_out;  // OR_Gate or_1, 4 bits wide
endmodule

module Multivibrador (
  input  E3,
  input  E2,
  input  E1,
  input  E0,
  input  Clockers,
  input  EN,
  input  Reset,
  output Saida
);

  wire and_1_out, and_2_out, and_3_out, and_4_out, d_ff_2_q, d_ff_3_q, d_ff_3_qn, d_ff_4_q, d_ff_5_q,
       d_ff_6_q, or_1_out, xnor_1_out, xnor_2_out, xnor_3_out, xnor_4_out, xor_1_out, xor_2_out, xor_3_out;

  D_Flip_Flop d_ff_1 (.D(EN), .clk(EN), .Q(Saida), .reset(or_1_out));  // open: Qn, preset
  D_Flip_Flop d_ff_2 (.D(Saida), .clk(Clockers), .Q(d_ff_2_q), .reset(or_1_out));  // open: Qn, preset
  and and_1 (and_1_out, Clockers, d_ff_2_q);
  D_Flip_Flop d_ff_3 (.D(d_ff_3_qn), .clk(and_1_out), .Q(d_ff_3_q), .Qn(d_ff_3_qn), .reset(or_1_out));  // open: preset
  xnor xnor_1 (xnor_1_out, E0, d_ff_3_q);
  xor xor_1 (xor_1_out, d_ff_3_q, d_ff_4_q);
  D_Flip_Flop d_ff_4 (.D(xor_1_out), .clk(and_1_out), .Q(d_ff_4_q), .reset(or_1_out));  // open: Qn, preset
  xnor xnor_2 (xnor_2_out, E1, d_ff_4_q);
  and and_2 (and_2_out, d_ff_3_q, d_ff_4_q);
  xor xor_2 (xor_2_out, and_2_out, d_ff_5_q);
  D_Flip_Flop d_ff_5 (.D(xor_2_out), .clk(and_1_out), .Q(d_ff_5_q), .reset(or_1_out));  // open: Qn, preset
  xnor xnor_3 (xnor_3_out, E2, d_ff_5_q);
  and and_3 (and_3_out, d_ff_3_q, d_ff_4_q, d_ff_5_q);
  xor xor_3 (xor_3_out, and_3_out, d_ff_6_q);
  D_Flip_Flop d_ff_6 (.D(xor_3_out), .clk(and_1_out), .Q(d_ff_6_q), .reset(or_1_out));  // open: Qn, preset
  or or_1 (or_1_out, and_4_out, Reset);
  xnor xnor_4 (xnor_4_out, E3, d_ff_6_q);
  and and_4 (and_4_out, xnor_1_out, xnor_2_out, xnor_3_out, xnor_4_out);
endmodule

module Registrador (
  input  INSERE_1,
  input  INSERE_0,
  input  RESET,
  output Q0,
  output Q1,
  output Q2,
  output Q3
);

  wire or_1_out;

  D_Flip_Flop d_ff_1 (.D(INSERE_1), .clk(or_1_out), .Q(Q0), .reset(RESET));  // open: Qn, preset
  D_Flip_Flop d_ff_2 (.D(Q0), .clk(or_1_out), .Q(Q1), .reset(RESET));  // open: Qn, preset
  or or_1 (or_1_out, INSERE_1, INSERE_0);
  D_Flip_Flop d_ff_3 (.D(Q1), .clk(or_1_out), .Q(Q2), .reset(RESET));  // open: Qn, preset
  D_Flip_Flop d_ff_4 (.D(Q2), .clk(or_1_out), .Q(Q3), .reset(RESET));  // open: Qn, preset
endmodule
